# Fritzing sketch Smart_Farm_Circuit (saved by Fritzing 0.9.3b)
breadboards: 1

parts:
  Part1 = Arduino Uno (Rev3)
  M1 = DC Motor
  Part2 = Bluetooth HC-05 Macho
  Part3 = MQ-4
  LCM1602_IIC1 = LCM1602 IIC [part_number="LCM1602 IIC" chip_label="LCM1602 IIC" package="DIP (Dual Inline) [THT]"]
  Part4 = Soil Moisture Sensor
  DHT1 = DHT11 Humitidy and Temperature Sensor
  Water_Level_Sensor1 = Water Level Sensor

nets:
  N1: Part1.A0, Part3.AO
  N2: Part1.A1, DHT1.DATA
  N3: Part1.A2, Water_Level_Sensor1.SIG
  N4: Part1.A3, Part4.SIG
  N5: Part1.A4/SDA, LCM1602_IIC1.SDA
  N6: Part1.A5/SCL, LCM1602_IIC1.SCL
  N7: Part1.D0/RX, Part2.RXD
  N8: Part1.D1/TX, Part2.TXD
  N9: Part1.D2, M1.pin_1
  VCC: Part1.5V, Part2.VCC, Part3.VCC, LCM1602_IIC1.VCC, Part4.VCC, DHT1.VDD, Water_Level_Sensor1.VCC
  GND: Part1.GND, M1.pin_2, Part2.GND, Part3.GND, LCM1602_IIC1.GND, Part4.GND, DHT1.GND, Water_Level_Sensor1.GND

custom parts:
  LCM1602 IIC: I2C-Module to use a 1602 or 2004 LCD on with the wire.h libory Serial LCD Modul
  DHT11 Humitidy and Temperature Sensor: DHT11 Humidity and Temperature Sensor
  Water Level Sensor: A water level sensor. This sensor operates at 3V to 5V. The Sig (signal) pin outputs an analogue signal that is in proportion to the amount of water in contact with the sensor.
